# Fritzing sketch EsquematicoSonda (saved by Fritzing 1.0.6)
breadboards: 1

parts:
  Componente1 = Arduino Nano (Rev3.0)
  U2 = SUP500F [package=sup500f]
  Componente2 = NCP1400 Step-Up Breakout
  Adafruit_BNO055_and_BMP280_BFF1 = Adafruit BNO055 and BMP280 BFF [mn=Adafruit mpn=#5937 part_number=#5937]
  BAT1 = Battery Holders [package=lipo-1100mAh]
  U3 = SUP500F [package=sup500f]

nets:
  GND: Componente1.GND, U2.GND, Componente2.GND, Adafruit_BNO055_and_BMP280_BFF1.GND, U3.GND
  N1: Componente1.D2, U3.RX-I
  N2: Componente1.D3, U3.TX-O
  N3: Componente1.D4, U2.RX-I
  N4: Componente1.D5, U2.TX-O
  5V: Componente1.5V, U3.VCC
  N5: Componente1.A5, Adafruit_BNO055_and_BMP280_BFF1.SCL
  N6: Componente1.A4, Adafruit_BNO055_and_BMP280_BFF1.SDA
  3V3: Componente1.3V3, U2.VCC, Adafruit_BNO055_and_BMP280_BFF1.3.3V
  N7: Componente2.VIN, BAT1.+, BAT1.-

notes:
  StepUp
  Gps Uart
  Bmp280
  Ard. Nano
  Lora Uart
